# Fritzing sketch sema (saved by Fritzing 0.9.3b)
breadboards: 1

parts:
  Parça1 = Breakout Board for Electret Microphone
  Parça2 = Bluetooth HC-05 Macho  # not connected
  Parça3 = Arduino Uno (Rev3) - ICSP
  U1 = RELAY [package=relay-jzc]

nets:
  VCC: Parça1.VCC, Parça3.5V, U1.COIL2
  GND: Parça1.GND, Parça3.GND, U1.NC
  N1: Parça1.AUD, Parça3.D4
  N2: Parça3.D5_PWM, U1.NO

notes:
  Bu kısma masa lambası gelecektir..
